# Fritzing sketch v2 - Minipro (saved by Fritzing 0.9.3b)
breadboards: 1

parts:
  Part4 = Bluetooth HM-10
  Part3 = Arduino Pro Mini (3.3V)
  T1 = LM35 Temperature Sensor [package="TO92 [THT]"]
  OLED_I2C1 = OLED 128x64 I2C Monochrome Display
  VCC1 = Battery block 9V
  R1 = Resistor [tolerance=±5% resistance=220 package=THT]
  M1 = MAX30102

nets:
  N1: Part4.RXD, Part3.TXO
  N2: Part4.TXD, Part3.RXI
  GND: Part4.GND, T1.GND, OLED_I2C1.GND, VCC1.-, M1.GND
  VCC: Part4.VCC, Part3.VCC, T1.+Vs, OLED_I2C1.VDD, M1.VIN
  N3: Part3.A4, OLED_I2C1.SDA, M1.SDA
  N4: Part3.A5, OLED_I2C1.SCK, M1.SCL
  N5: Part3.RAW, VCC1.+
  N6: Part3.GND, R1.Pin_1
  N7: Part3.A1, T1.Vout, R1.Pin_0

custom parts:
  MAX30102: Oximeter module using the MAX30102 chip. You may wish to read (and check your module) this post on power problems with these modules: https://reedpaper.wordpress.com/2018/08/22/pulse-oximeter-max30100-max30102-how-to-fix-wrong-board/ . As usual, if you want the mounting holes in pcb, you need to drag a hole over the pad in silkscreen to actually drill the hole (by default they are not drilled)
