# Fritzing sketch v4 - Nodemcu (saved by Fritzing 0.9.3b)
breadboards: 1

parts:
  M1 = MAX30102
  U1 = MLX90614 [package=to-39]
  U2 = NodeMCU V1.0

nets:
  VIN: M1.VIN, U1.VDD, U2.3V3
  N1: M1.SCL, U1.SCL_VZ, U2.D2
  N2: M1.SDA, U1.PWM_SDA, U2.D1
  N3: M1.INT, U2.D0
  GND: M1.GND, U1.VSS, U2.GND

custom parts:
  MAX30102: Oximeter module using the MAX30102 chip. You may wish to read (and check your module) this post on power problems with these modules: https://reedpaper.wordpress.com/2018/08/22/pulse-oximeter-max30100-max30102-how-to-fix-wrong-board/ . As usual, if you want the mounting holes in pcb, you need to drag a hole over the pad in silkscreen to actually drill the hole (by default they are not drilled)
  NodeMCU V1.0: ESP8266 based NodeMCU
